# Fritzing sketch merpati (saved by Fritzing 0.9.3b)
breadboards: 2

parts:
  Part1 = Arduino Uno (Rev3)
  U1 = ESP8266 NodeMCU LoLin module
  125_kHz_RFID_module1 = RDM6300
  A1 = NEO-6M GPS Module [part_number=GY-GPS6MV2]
  A2 = mini boost module
  LED1 = LED - 3mm [color="Red (633nm)" package="3 mm [THT]"]
  R1 = Resistor [tolerance=±5% resistance=330 package="0805 [SMD]"]
  BAT1 = 18650 battery holder [package=battery-18650-kit]
  U2 = SWITCH-SPST-2 [package=r_sw_th]
  Part2 = RDM6300-ANT
  U3 = ESP8266 NodeMCU LoLin module
  A3 = NEO-6M GPS Module [part_number=GY-GPS6MV2]
  A4 = mini boost module
  BAT2 = 18650 battery holder [package=battery-18650-kit]
  U4 = SWITCH-SPST-2 [package=r_sw_th]
  LED2 = LED - 3mm [color="Red (633nm)" package="3 mm [THT]"]
  R2 = Resistor [tolerance=±5% resistance=330 package="0805 [SMD]"]
  LED3 = LED - 3mm [color="Yellow (595nm)" package="3 mm [THT]"]
  LED4 = LED - 3mm [color="Green (570nm)" package="3 mm [THT]"]
  S1 = Round Pushbutton
  S2 = Round Pushbutton
  R3 = Resistor [tolerance=±5% resistance=330 package="0805 [SMD]"]
  R4 = Resistor [tolerance=±5% resistance=330 package="0805 [SMD]"]

nets:
  GND: Part1.GND, U1.GND, 125_kHz_RFID_module1.GND#60, A1.GND, A2.Pin_3, R1.Pin_1
  N1: Part1.D1/TX, U1.D7
  N2: Part1.D6_PWM, 125_kHz_RFID_module1.TX, 125_kHz_RFID_module1.GND#66, 125_kHz_RFID_module1.GND#67
  5V: Part1.5V, U1.Vin, 125_kHz_RFID_module1.+5V, LED1.anode, U2.O
  N3: U1.D1, A1.Rx
  N4: U1.D2, A1.Tx
  3V3: U1.3V3, A1.Vcc
  N5: 125_kHz_RFID_module1.ANT1, Part2.ANT1
  N6: 125_kHz_RFID_module1.ANT2, Part2.ANT2
  N7: A2.Pin_1, BAT1.+
  N8: A2.Pin_2, BAT1.-
  N9: A2.Pin_4, U2.P
  N10: LED1.cathode, R1.Pin_0
  N11: U3.D1, A3.Rx
  N12: U3.D2, A3.Tx
  N13: U3.D3, R3.Pin_0
  N14: U3.D4, R4.Pin_0
  3V3_2: U3.3V3, A3.Vcc
  GND_2: U3.GND, A3.GND, A4.Pin_3
  N15: U3.D5, S1.leg1
  N16: U3.D6, S2.leg1
  N17: U3.Vin, A4.Pin_4
  N18: A4.Pin_1, BAT2.+
  N19: A4.Pin_2, U4.O
  N20: BAT2.-, U4.P
  N21: LED2.cathode, LED3.cathode, LED4.cathode, S1.leg0, S2.leg0
  N22: LED2.anode, R2.Pin_1
  N23: LED3.anode, R3.Pin_1
  N24: LED4.anode, R4.Pin_1

notes:
  REMOTE
  TERBANG
  LOKASI

custom parts:
  ESP8266 NodeMCU LoLin module: ESP8266 based NodeMCU
  RDM6300: 125 kHz RFID module (serial interface)
  NEO-6M GPS Module: GY-GPS6MV2 NEO-6M GPS Module Module based on U-blox NEO-6M GPS engine, incorporating regulator for 3.3-5V DC input, MS621FE-compatible rechargeable battery for backup and EEPROM for storing configuration settings. Links: NEO-6 series product information page NEO-6 Datasheet
  mini boost module: mini boost module.
  18650 battery holder: 18650 Battery
  RDM6300-ANT: Antenna
